// Logisim project ioradiX_version1.1.circ as structural Verilog
// 10bit reg
module _10bitreg (
  input  [1:0] read_value01,
  input  [9:0] Data_input,
  input  [1:0] decoder_select__write_reg,
  input  Read_Write,
  input  clock,
  input  [1:0] Read_value_02,
  output [9:0] out_7,
  output [9:0] out_8
);

  wire and_1_out, and_2_out, and_3_out, and_4_out, decoder_1_out0, decoder_1_out1, decoder_1_out2,
       decoder_1_out3, not_1_out;
  wire [9:0] register_1_q, register_2_q, register_3_q, register_4_q;

  not not_1 (not_1_out, clock);
  Decoder #(.select(2), .enable("false")) decoder_1 (
    .out0(decoder_1_out0), .out1(decoder_1_out1), .out2(decoder_1_out2), .out3(decoder_1_out3),
    .sel(decoder_select__write_reg));
  and and_1 (and_1_out, decoder_1_out0, Read_Write);
  and and_2 (and_2_out, decoder_1_out1, Read_Write);
  and and_3 (and_3_out, decoder_1_out2, Read_Write);
  and and_4 (and_4_out, decoder_1_out3, Read_Write);
  Register #(.width(10)) register_1 (.D(Data_input), .en(and_1_out), .Q(register_1_q), .clk(not_1_out));  // open: clr
  Register #(.width(10)) register_2 (.D(Data_input), .en(and_2_out), .Q(register_2_q), .clk(not_1_out));  // open: clr
  Register #(.width(10)) register_3 (.D(Data_input), .en(and_3_out), .Q(register_3_q), .clk(not_1_out));  // open: clr
  Register #(.width(10)) register_4 (.D(Data_input), .en(and_4_out), .Q(register_4_q), .clk(not_1_out));  // open: clr
  Multiplexer #(.select(2), .width(10), .enable("false")) multiplexer_1 (
    .in0(register_1_q), .in1(register_2_q), .in2(register_3_q), .in3(register_4_q), .out(out_7),
    .sel(read_value01));
  Multiplexer #(.select(2), .width(10), .enable("false")) multiplexer_2 (
    .in0(register_1_q), .in1(register_2_q), .in2(register_3_q), .in3(register_4_q), .out(out_8),
    .sel(Read_value_02));
endmodule

// 10 bit alu
module _10bitalu (
  input  add_sub,
  input  Carry_in,
  input  [1:0] operations,
  input  [9:0] A,
  input  [9:0] B,
  output Result_is_zero,
  output [9:0] Result,
  output Over_flow,
  output carry_out
);

  wire cary, n1bitalu_1_carry_out, n1bitalu_3_carry_out, n1bitalu_4_carry_out, n1bitalu_5_carry_out,
       n1bitalu_6_carry_out, n1bitalu_7_carry_out, n1bitalu_8_carry_out, n1bitalu_9_carry_out;

  _1bitalu u_1bitalu_1 (
    .sub_add(add_sub), .out_put(Result[0]), .carry_out(n1bitalu_1_carry_out), .Carry_in(Carry_in),
    .op_select(operations), .input_B(B[0]), .input_a(A[0]));
  _1bitalu u_1bitalu_2 (
    .sub_add(add_sub), .out_put(Result[1]), .carry_out(cary), .Carry_in(n1bitalu_1_carry_out),
    .op_select(operations), .input_B(B[1]), .input_a(A[1]));
  _1bitalu u_1bitalu_3 (
    .sub_add(add_sub), .out_put(Result[2]), .carry_out(n1bitalu_3_carry_out), .Carry_in(cary),
    .op_select(operations), .input_B(B[2]), .input_a(A[2]));
  _1bitalu u_1bitalu_4 (
    .sub_add(add_sub), .out_put(Result[3]), .carry_out(n1bitalu_4_carry_out),
    .Carry_in(n1bitalu_3_carry_out), .op_select(operations), .input_B(B[3]), .input_a(A[3]));
  _1bitalu u_1bitalu_5 (
    .sub_add(add_sub), .out_put(Result[4]), .carry_out(n1bitalu_5_carry_out),
    .Carry_in(n1bitalu_4_carry_out), .op_select(operations), .input_B(B[4]), .input_a(A[4]));
  _1bitalu u_1bitalu_6 (
    .sub_add(add_sub), .out_put(Result[5]), .carry_out(n1bitalu_6_carry_out),
    .Carry_in(n1bitalu_5_carry_out), .op_select(operations), .input_B(B[5]), .input_a(A[5]));
  _1bitalu u_1bitalu_7 (
    .sub_add(add_sub), .out_put(Result[6]), .carry_out(n1bitalu_7_carry_out),
    .Carry_in(n1bitalu_6_carry_out), .op_select(operations), .input_B(B[6]), .input_a(A[6]));
  _1bitalu u_1bitalu_8 (
    .sub_add(add_sub), .out_put(Result[7]), .carry_out(n1bitalu_8_carry_out),
    .Carry_in(n1bitalu_7_carry_out), .op_select(operations), .input_B(B[7]), .input_a(A[7]));
  _1bitalu u_1bitalu_9 (
    .sub_add(add_sub), .out_put(Result[8]), .carry_out(n1bitalu_9_carry_out),
    .Carry_in(n1bitalu_8_carry_out), .op_select(operations), .input_B(B[8]), .input_a(A[8]));
  _1bitalu u_1bitalu_10 (
    .sub_add(add_sub), .out_put(Result[9]), .carry_out(carry_out), .Carry_in(n1bitalu_9_carry_out),
    .op_select(operations), .input_B(B[9]), .input_a(A[9]));
  nor nor_1 (Result_is_zero, Result[0], Result[1], Result[2], Result[3], Result[4], Result[6], Result[7], Result[8], Result[9], Result[5]);
  xor xor_1 (Over_flow, n1bitalu_9_carry_out, carry_out);

  // Other names for the same wires on the sheet: _6 = A[0]; _7 = A[1]; _8 = A[2]; _9 = A[3]; _10 = A[4]; _11 = A[5];
  //   _12 = A[6]; _13 = A[7]; _14 = A[8]; _15 = A[9]; g = B[0]; h = B[1]; i = B[2]; j = B[3]; k = B[4]; l = B[5];
  //   m = B[6]; n = B[7]; o = B[8]; p = B[9]
endmodule

module _1bitalu (
  input  Carry_in,
  input  [1:0] op_select,
  input  input_B,
  input  input_a,
  input  sub_add,
  output out_put,
  output carry_out
);

  wire adder_1_out, and_1_out, multiplexer_1_out, not_1_out, or_1_out;

  not not_1 (not_1_out, input_B);
  Multiplexer #(.enable("false")) multiplexer_1 (
    .in0(input_B), .in1(not_1_out), .out(multiplexer_1_out), .sel(sub_add));
  and and_1 (and_1_out, input_a, input_B);
  or or_1 (or_1_out, input_a, input_B);
  Adder #(.width(1)) adder_1 (.a(input_a), .b(multiplexer_1_out), .out(adder_1_out), .cin(Carry_in), .cout(carry_out));
  Multiplexer #(.select(2), .enable("false")) multiplexer_2 (
    .in0(and_1_out), .in1(or_1_out), .in2(adder_1_out), .in3(adder_1_out), .out(out_put), .sel(op_select));
endmodule

module _10bitprocessor (
  input  read_write,
  input  in_2,
  output out_3,
  output out_4,
  output out_5,
  output out_6,
  output out_7,
  output out_8,
  output out_9,
  output out_10,
  output out_11,
  output out_12,
  output [1:0] RD,
  output [1:0] RT,
  output [1:0] RS,
  output [9:0] out_16,
  output [9:0] out_17,
  output [9:0] Alu_output,
  output out_19,
  output out_20,
  output out_21,
  output [9:0] out_22
);

  wire A, L, m3, m4, ml, o, R_W, S;
  wire [1:0] multiplexer_2_out, multiplexer_3_out, multiplexer_7_out;
  wire [9:0] adder_1_out, adder_2_out, multiplexer_1_out, multiplexer_4_out, multiplexer_5_out,
       multiplexer_6_out, n10bitreg_1_out_8, register_1_q;

  ControlUnit controlunit_1 (
    .in_1({out_3, out_4, out_5, out_6}), .Mux3_pc(m3), .Add_sub_cin(A), .load(L), .store(S), .in_2(out_19),
    .Mux3_load(ml), .mux_alu_reg(o), .read_write(R_W), .mux4_load_store(m4));
  Register #(.width(10)) register_1 (.D(multiplexer_1_out), .Q(register_1_q), .clk(in_2));  // open: en, clr
  Adder #(.width(10)) adder_1 (.a(10'h1), .b(register_1_q), .out(adder_1_out));  // open: cin, cout
  Multiplexer #(.width(10), .enable("false")) multiplexer_1 (
    .in0(adder_1_out), .in1(adder_2_out), .out(multiplexer_1_out), .sel(m3));
  ROM #(.addrWidth(10), .dataWidth(10)) rom_1 (
    .addr(register_1_q), .data({out_3, out_4, out_5, out_6, out_7, out_8, out_9, out_10, out_11, out_12}));  // open: sel
  Multiplexer #(.width(2), .enable("false")) multiplexer_2 (
    .in0({out_7, out_8}), .in1({out_9, out_10}), .out(multiplexer_2_out), .sel(L));
  Multiplexer #(.width(2), .enable("false")) multiplexer_3 (
    .in0({out_11, out_12}), .in1(multiplexer_2_out), .out(multiplexer_3_out), .sel(o));
  _10bitreg u_10bitreg_1 (
    .Data_input(multiplexer_4_out), .read_value01({out_7, out_8}),
    .decoder_select__write_reg(multiplexer_3_out), .Read_Write(R_W), .Read_value_02({out_9, out_10}),
    .out_7(out_17), .out_8(n10bitreg_1_out_8), .clock(in_2));
  assign out_22 = {{8{1'b0}}, {out_11, out_12}};  // Bit_Extender bit_extender_1
  Multiplexer #(.width(10), .enable("false")) multiplexer_4 (
    .in0(Alu_output), .in1(out_16), .out(multiplexer_4_out), .sel(ml));
  DataMemory datamemory_1 (
    .ADDRESS(Alu_output), .value_input(out_17), .Store(S), .load(L), .data_output(out_16), .clk(in_2));
  Multiplexer #(.width(10), .enable("false")) multiplexer_5 (
    .in0(out_17), .in1(n10bitreg_1_out_8), .out(multiplexer_5_out), .sel(S));
  Multiplexer #(.width(10), .enable("false")) multiplexer_6 (
    .in0(n10bitreg_1_out_8), .in1(out_22), .out(multiplexer_6_out), .sel(o));
  Multiplexer #(.width(2), .enable("false")) multiplexer_7 (
    .in0({out_5, out_6}), .in1(2'b10), .out(multiplexer_7_out), .sel(S));
  _10bitalu u_10bitalu_1 (
    .add_sub(A), .Carry_in(A), .A(multiplexer_5_out), .B(multiplexer_6_out), .operations(multiplexer_7_out),
    .Result_is_zero(out_19), .Result(Alu_output), .Over_flow(out_20), .carry_out(out_21));
  Adder #(.width(10)) adder_2 (.a(adder_1_out), .b({out_22[8:0], read_write}), .out(adder_2_out));  // open: cin, cout

  assign RD = {out_11, out_12};
  assign RS = {out_7, out_8};
  assign RT = {out_9, out_10};

  // Notes on the sheet:
  //   contents of rom_1 (hex, n*v repeats v):
  //   0 3a4 389 3da 9b 373 0 0 db 373
endmodule

module DataMemory (
  input  [9:0] ADDRESS,
  input  [9:0] value_input,
  input  Store,
  input  clk,
  input  load,
  output [9:0] data_output
);

  wire not_1_out;

  not not_1 (not_1_out, clk);
  RAM #(.addrWidth(10), .dataWidth(10), .bus("separate")) ram_1 (
    .addr(ADDRESS), .din(value_input), .data(data_output), .str(Store), .clk(not_1_out), .ld(load));  // open: sel, clr
endmodule

module ControlUnit (
  input  [3:0] in_1,
  input  in_2,
  output Mux3_pc,
  output Add_sub_cin,
  output mux4_load_store,
  output load,
  output store,
  output Mux3_load,
  output read_write,
  output mux_alu_reg
);

  wire and_1_out, and_2_out, and_3_out, and_4_out, not_1_out, not_2_out, not_3_out, not_4_out, not_5_out,
       or_3_out;

  not not_1 (not_1_out, in_2);
  not not_2 (not_2_out, in_1[3]);
  not not_3 (not_3_out, in_1[2]);
  not not_4 (not_4_out, in_1[1]);
  not not_5 (not_5_out, in_1[0]);
  and and_1 (and_1_out, not_3_out, not_2_out, in_1[1], in_1[0]);
  and and_2 (and_2_out, in_1[3], in_1[1], in_1[0]);
  and and_3 (and_3_out, not_5_out, in_1[1], in_1[3]);
  and and_4 (and_4_out, in_1[0], in_1[1], not_2_out);
  and and_5 (Mux3_pc, in_2, in_1[3], in_1[2], in_1[1], in_1[0]);
  or or_1 (Add_sub_cin, and_1_out, and_2_out);
  and and_6 (load, in_1[3], in_1[2], in_1[1], not_5_out);
  and and_7 (store, in_1[3], in_1[2], not_4_out, in_1[0]);
  and and_8 (Mux3_load, in_1[2], in_1[3], in_1[1], not_5_out);
  or or_2 (read_write, and_3_out, and_4_out, not_3_out);
  or or_3 (or_3_out, not_5_out, not_4_out, not_3_out);
  and and_9 (mux_alu_reg, or_3_out, in_1[3]);
  or or_4 (mux4_load_store, load, store);
endmodule
